// Logisim project cpu.circ as structural Verilog: 7 circuits, main circuit main
module main (
);

  wire AddI, AluSrc, And, and_1_out, and_2_out, Beq, Clock, Jump, Load, MemRead, MemToReg, MemWrite, Mult,
       not_1_out, not_2_out, not_3_out, not_4_out, not_5_out, not_6_out, not_7_out, Or, or_1_out, or_2_out,
       or_3_out, or_4_out, RegDest, Reset_2_out, Reset_3_out, Reset_out, ResetAll, Resta, Store, Suma,
       Tipo_J, WriteData, Zero;
  wire [1:0] AluOp, controlled_buffer_8_out_5;
  wire [3:0] adder_1_out_2, AluSel, bit_extender_1_out, bit_extender_3_out, bit_extender_5_out,
       bit_extender_7_out, controlled_buffer_1_out_2, controlled_buffer_1_out_3, controlled_buffer_1_out_4,
       controlled_buffer_1_out_5, controlled_buffer_5_out_2, controlled_buffer_5_out_3,
       controlled_buffer_5_out_4, controlled_buffer_5_out_5, controlled_buffer_5_out_6,
       controlled_buffer_6_out, controlled_buffer_6_out_2, controlled_buffer_6_out_3,
       controlled_buffer_6_out_4, controlled_buffer_8_out_2, controlled_buffer_8_out_3,
       controlled_buffer_8_out_4, controlled_buffer_9_out_2, controlled_buffer_9_out_3,
       controlled_buffer_9_out_4, controlled_buffer_9_out_5, controlled_buffer_9_out_6;
  wire [4:0] controlled_buffer_2_out, controlled_buffer_3_out, controlled_buffer_4_out, multiplexer_3_out,
       Rd, Rs, Rt;
  wire [5:0] Funct, Opcode;
  wire [11:0] controlled_buffer_5_out, controlled_buffer_8_out, controlled_buffer_9_out;
  wire [15:0] Address;
  wire [23:0] bit_extender_6_out;
  wire [25:0] JAddress;
  wire [27:0] adder_1_out, Data, JAddress28;
  wire [31:0] Acum, adder_2_out, Address32, AluData, controlled_buffer_1_out, controlled_buffer_7_out,
       multiplexer_1_out, multiplexer_4_out, register_1_q, Result, rom_1_data, RsOut, RtOut;

  Multiplexer #(.width(32), .disabled(0), .enable("false")) multiplexer_1 (
    .in0(Acum), .in1({adder_1_out_2, JAddress28}), .out(multiplexer_1_out), .sel(Tipo_J));
  Clock clock_1 (.out(Clock));
  Hex_Digit_Display hex_digit_display_1 (.value(controlled_buffer_1_out[31:28]));  // open: dp
  Register #(.width(32), .trigger("falling")) register_1 (
    .D(multiplexer_1_out), .Q(register_1_q), .clk(Clock), .clr(or_1_out));  // open: en
  or or_1 (or_1_out, Reset_out, ResetAll);
  Button Reset (.out(Reset_out));
  Button Reset_All (.out(ResetAll));
  _7_Segment_Display u_7_segment_display_1 (
    .g(Data[24]), .f(Data[23]), .a(Data[22]), .b(Data[21]), .e(Data[25]), .d(Data[26]), .c(Data[27]));  // open: dp
  display Display (
    .Funct(Funct), .OpCode(Opcode), .Tipo_R(RegDest), .Suma(Suma), .Resta(Resta), .And(And), .Or(Or),
    .Mult(Mult), .Beq(Beq), .AddI(AddI), .Load(Load), .Store(Store), .Jump(Jump), .Data(Data));
  Hex_Digit_Display hex_digit_display_2 (.value(controlled_buffer_1_out_5));  // open: dp
  Adder #(.width(32)) adder_1 (.a(32'h1), .b(register_1_q), .out({adder_1_out_2, adder_1_out}));  // open: cin, cout
  _7_Segment_Display u_7_segment_display_2 (
    .g(Data[17]), .f(Data[16]), .a(Data[15]), .b(Data[14]), .e(Data[18]), .d(Data[19]), .c(Data[20]));  // open: dp
  Hex_Digit_Display hex_digit_display_3 (.value(controlled_buffer_1_out_3));  // open: dp
  Hex_Digit_Display hex_digit_display_4 (.value(controlled_buffer_1_out_4));  // open: dp
  _7_Segment_Display u_7_segment_display_3 (
    .g(Data[10]), .f(Data[9]), .a(Data[8]), .b(Data[7]), .e(Data[11]), .d(Data[12]), .c(Data[13]));  // open: dp
  Hex_Digit_Display hex_digit_display_5 (.value(controlled_buffer_1_out_2));  // open: dp
  assign {controlled_buffer_1_out[31:28], controlled_buffer_1_out_5, controlled_buffer_1_out_4, controlled_buffer_1_out_3, controlled_buffer_1_out_2, controlled_buffer_1_out[11:0]} = not_2_out ? RsOut : 32'bz;  // Controlled_Buffer controlled_buffer_1
  ROM #(.addrWidth(24), .dataWidth(32)) rom_1 (.addr(register_1_q[23:0]), .data(rom_1_data));  // open: sel
  _7_Segment_Display u_7_segment_display_4 (
    .g(Data[3]), .f(Data[2]), .a(Data[1]), .b(Data[0]), .e(Data[4]), .d(Data[5]), .c(Data[6]));  // open: dp
  assign controlled_buffer_2_out = not_1_out ? Rs : 5'bz;  // Controlled_Buffer controlled_buffer_2
  not not_1 (not_1_out, Jump);
  Hex_Digit_Display hex_digit_display_6 (.value(controlled_buffer_1_out[11:8]));  // open: dp
  not not_2 (not_2_out, Jump);
  Adder #(.width(32)) adder_2 (.a({adder_1_out_2, adder_1_out}), .b(Address32), .out(adder_2_out));  // open: cin, cout
  decoder Decoder (
    .Instruction(rom_1_data), .Address(Address), .Funct(Funct), .Rd(Rd), .Rt(Rt), .Rs(Rs), .OpCode(Opcode),
    .JAddress(JAddress));
  Button Reset_2 (.out(Reset_2_out));
  Hex_Digit_Display hex_digit_display_7 (.value(controlled_buffer_2_out[3:0]));  // open: dp
  Hex_Digit_Display hex_digit_display_8 (.value(bit_extender_1_out));  // open: dp
  assign bit_extender_1_out = {{3{1'b0}}, controlled_buffer_2_out[4]};  // Bit_Extender bit_extender_1
  Hex_Digit_Display hex_digit_display_9 (.value(controlled_buffer_1_out[7:4]));  // open: dp
  Hex_Digit_Display hex_digit_display_10 (.value(controlled_buffer_1_out[3:0]));  // open: dp
  Multiplexer #(.width(32), .disabled(0), .enable("false")) multiplexer_2 (
    .in0({adder_1_out_2, adder_1_out}), .in1(adder_2_out), .out(Acum), .sel(and_1_out));
  and and_1 (and_1_out, Beq, Zero);
  or or_2 (or_2_out, Reset_2_out, ResetAll);
  assign JAddress28 = {{2{1'b0}}, JAddress};  // Bit_Extender bit_extender_2
  Hex_Digit_Display hex_digit_display_11 (.value(bit_extender_3_out));  // open: dp
  assign controlled_buffer_3_out = not_3_out ? Rt : 5'bz;  // Controlled_Buffer controlled_buffer_3
  not not_3 (not_3_out, Jump);
  Hex_Digit_Display hex_digit_display_12 (.value(controlled_buffer_5_out_6));  // open: dp
  Multiplexer #(.width(5), .enable("false")) multiplexer_3 (.in0(Rt), .in1(Rd), .out(multiplexer_3_out), .sel(RegDest));
  Hex_Digit_Display hex_digit_display_13 (.value(controlled_buffer_3_out[3:0]));  // open: dp
  assign bit_extender_3_out = {{3{1'b0}}, controlled_buffer_3_out[4]};  // Bit_Extender bit_extender_3
  Hex_Digit_Display hex_digit_display_14 (.value(controlled_buffer_5_out_5));  // open: dp
  control Control (
    .OpCode(Opcode), .Reg_Dest(RegDest), .Branch(Beq), .MemRead(MemRead), .MemtoReg(MemToReg), .AluOP(AluOp),
    .MemWrite(MemWrite), .Alu_Src(AluSrc), .RegWrite(WriteData), .Jump(Tipo_J));
  registers Registros (
    .Rs(Rs), .Rt(Rt), .RsOut(RsOut), .RtOut(RtOut), .Clock(Clock), .Reg_Write(WriteData),
    .Write_Data(Result), .Write_Reg(multiplexer_3_out), .Reset(or_2_out));
  assign Address32 = {{16{Address[15]}}, Address};  // Bit_Extender bit_extender_4
  Hex_Digit_Display hex_digit_display_15 (.value(controlled_buffer_4_out[3:0]));  // open: dp
  Hex_Digit_Display hex_digit_display_16 (.value(bit_extender_5_out));  // open: dp
  assign bit_extender_5_out = {{3{1'b0}}, controlled_buffer_4_out[4]};  // Bit_Extender bit_extender_5
  assign controlled_buffer_4_out = RegDest ? Rd : 5'bz;  // Controlled_Buffer controlled_buffer_4
  Hex_Digit_Display hex_digit_display_17 (.value(controlled_buffer_5_out_3));  // open: dp
  Hex_Digit_Display hex_digit_display_18 (.value(controlled_buffer_5_out_4));  // open: dp
  Hex_Digit_Display hex_digit_display_19 (.value(controlled_buffer_6_out_4));  // open: dp
  Hex_Digit_Display hex_digit_display_20 (.value(controlled_buffer_5_out_2));  // open: dp
  assign {controlled_buffer_5_out_6, controlled_buffer_5_out_5, controlled_buffer_5_out_4, controlled_buffer_5_out_3, controlled_buffer_5_out_2, controlled_buffer_5_out} = not_4_out ? RtOut : 32'bz;  // Controlled_Buffer controlled_buffer_5
  Multiplexer #(.width(32), .enable("false")) multiplexer_4 (
    .in0(RtOut), .in1(Address32), .out(multiplexer_4_out), .sel(AluSrc));
  control_alu Alu_Control (.AluOP(AluOp), .Funct(Funct), .Alu_Sel(AluSel));
  Hex_Digit_Display hex_digit_display_21 (.value(controlled_buffer_6_out_3));  // open: dp
  Hex_Digit_Display hex_digit_display_22 (.value(controlled_buffer_5_out[11:8]));  // open: dp
  not not_4 (not_4_out, Jump);
  ALU ALU (.Alu_Sel(AluSel), .Rs(RsOut), .Rt_Imm(multiplexer_4_out), .Zero(Zero), .Resul(AluData));
  Hex_Digit_Display hex_digit_display_23 (.value(controlled_buffer_6_out_2));  // open: dp
  assign {controlled_buffer_6_out_4, controlled_buffer_6_out_3, controlled_buffer_6_out_2, controlled_buffer_6_out} = and_2_out ? Address : 16'bz;  // Controlled_Buffer controlled_buffer_6
  not not_5 (not_5_out, RegDest);
  and and_2 (and_2_out, not_5_out, not_6_out);
  not not_6 (not_6_out, Jump);
  Hex_Digit_Display hex_digit_display_24 (.value(controlled_buffer_5_out[7:4]));  // open: dp
  Hex_Digit_Display hex_digit_display_25 (.value(controlled_buffer_5_out[3:0]));  // open: dp
  Bit_Extender #(.in_width(32), .out_width(24)) bit_extender_6 (.in(AluData), .out(bit_extender_6_out));
  Hex_Digit_Display hex_digit_display_26 (.value(controlled_buffer_6_out));  // open: dp
  Hex_Digit_Display hex_digit_display_27 (.value(bit_extender_7_out));  // open: dp
  assign bit_extender_7_out = {{2{1'b0}}, controlled_buffer_8_out_5};  // Bit_Extender bit_extender_7
  Hex_Digit_Display hex_digit_display_28 (.value(controlled_buffer_9_out_6));  // open: dp
  Hex_Digit_Display hex_digit_display_29 (.value(controlled_buffer_9_out_5));  // open: dp
  assign controlled_buffer_7_out = MemWrite ? RtOut : 32'bz;  // Controlled_Buffer controlled_buffer_7
  Hex_Digit_Display hex_digit_display_30 (.value(controlled_buffer_8_out_4));  // open: dp
  Hex_Digit_Display hex_digit_display_31 (.value(controlled_buffer_8_out_3));  // open: dp
  Hex_Digit_Display hex_digit_display_32 (.value(controlled_buffer_9_out_4));  // open: dp
  not not_7 (not_7_out, Clock);
  or or_3 (or_3_out, MemWrite, MemRead);
  Hex_Digit_Display hex_digit_display_33 (.value(controlled_buffer_8_out_2));  // open: dp
  assign {controlled_buffer_8_out_5, controlled_buffer_8_out_4, controlled_buffer_8_out_3, controlled_buffer_8_out_2, controlled_buffer_8_out} = Jump ? JAddress : 26'bz;  // Controlled_Buffer controlled_buffer_8
  Hex_Digit_Display hex_digit_display_34 (.value(controlled_buffer_9_out_3));  // open: dp
  Hex_Digit_Display hex_digit_display_35 (.value(controlled_buffer_9_out_2));  // open: dp
  RAM #(.addrWidth(24), .dataWidth(32)) ram_1 (
    .addr(bit_extender_6_out), .data(controlled_buffer_7_out), .sel(or_3_out), .clk(not_7_out), .ld(MemRead),
    .clr(or_4_out));
  or or_4 (or_4_out, Reset_3_out, ResetAll);
  Hex_Digit_Display hex_digit_display_36 (.value(controlled_buffer_8_out[11:8]));  // open: dp
  Hex_Digit_Display hex_digit_display_37 (.value(controlled_buffer_9_out[11:8]));  // open: dp
  assign {controlled_buffer_9_out_6, controlled_buffer_9_out_5, controlled_buffer_9_out_4, controlled_buffer_9_out_3, controlled_buffer_9_out_2, controlled_buffer_9_out} = RegDest ? AluData : 32'bz;  // Controlled_Buffer controlled_buffer_9
  Multiplexer #(.width(32), .enable("false")) multiplexer_5 (
    .in0(AluData), .in1(controlled_buffer_7_out), .out(Result), .sel(MemToReg));
  Button Reset_3 (.out(Reset_3_out));
  Hex_Digit_Display hex_digit_display_38 (.value(controlled_buffer_8_out[3:0]));  // open: dp
  Hex_Digit_Display hex_digit_display_39 (.value(controlled_buffer_8_out[7:4]));  // open: dp
  Hex_Digit_Display hex_digit_display_40 (.value(controlled_buffer_9_out[7:4]));  // open: dp
  Hex_Digit_Display hex_digit_display_41 (.value(controlled_buffer_9_out[3:0]));  // open: dp

  // Notes on the sheet:
  //   Instruction
  //   Rs Info
  //   contents of rom_1 (hex, n*v repeats v):
  //   21290001 214a0002 216b0003 216c0001 12a4020 10b5820 1896022 1094024 12a4825 ac080004 ac090003
  //   ac0a0002 ac0b0001 ac0c0000 8c080000 8c090001 8c0a0002 8c0b0003 8c0c0004 110b0004 8000005
  //   rs
  //   rt
  //   rd
  //   Rt Info
  //   Address/Imm
  //   Jump Address
  //   Rd Info
endmodule

module decoder (
  input  [31:0] Instruction,
  output [15:0] Address,
  output [5:0] Funct,
  output [4:0] Rd,
  output [4:0] Rt,
  output [4:0] Rs,
  output [5:0] OpCode,
  output [25:0] JAddress
);


  assign Address = Instruction[15:0];
  assign Funct = Instruction[5:0];
  assign JAddress = Instruction[25:0];
  assign OpCode = Instruction[31:26];
  assign Rd = Instruction[15:11];
  assign Rs = Instruction[25:21];
  assign Rt = Instruction[20:16];
endmodule

module registers (
  input  [4:0] Rs,
  input  [4:0] Rt,
  input  Reg_Write,
  input  [4:0] Write_Reg,
  input  Clock,
  input  [31:0] Write_Data,
  input  Reset,
  output [31:0] RsOut,
  output [31:0] RtOut
);

  wire R0_W, R1_W, R2_W, R3_W, R4_W, R5_W, R6_W, R7_W, R8_W, R9_W, R10_W, R11_W, R12_W, R13_W, R14_W, R15_W,
       R16_W, R17_W, R18_W, R19_W, R20_W, R21_W, R22_W, R23_W, R24_W, R25_W, R26_W, R27_W, R28_W, R29_W,
       R30_W, R31_W;
  wire [4:0] controlled_buffer_2_out;
  wire [31:0] R0, R1, R2, R3, R4, R5, R6, R7, R8, R9, R10, R11, R12, R13, R14, R15, R16, R17, R18, R19, R20,
       R21, R22, R23, R24, R25, R26, R27, R28, R29, R30, R31, Res;

  Register #(.width(32)) register_1 (.D(Res), .en(R0_W), .Q(R0), .clk(Clock), .clr(Reset));
  Register #(.width(32)) register_2 (.D(Res), .en(R1_W), .Q(R1), .clk(Clock), .clr(Reset));
  Register #(.width(32)) register_3 (.D(Res), .en(R2_W), .Q(R2), .clk(Clock), .clr(Reset));
  Register #(.width(32)) register_4 (.D(Res), .en(R3_W), .Q(R3), .clk(Clock), .clr(Reset));
  Register #(.width(32)) register_5 (.D(Res), .en(R4_W), .Q(R4), .clk(Clock), .clr(Reset));
  Register #(.width(32)) register_6 (.D(Res), .en(R5_W), .Q(R5), .clk(Clock), .clr(Reset));
  Register #(.width(32)) register_7 (.D(Res), .en(R6_W), .Q(R6), .clk(Clock), .clr(Reset));
  Register #(.width(32)) register_8 (.D(Res), .en(R7_W), .Q(R7), .clk(Clock), .clr(Reset));
  Register #(.width(32)) register_9 (.D(Res), .en(R8_W), .Q(R8), .clk(Clock), .clr(Reset));
  Register #(.width(32)) register_10 (.D(Res), .en(R9_W), .Q(R9), .clk(Clock), .clr(Reset));
  Register #(.width(32)) register_11 (.D(Res), .en(R10_W), .Q(R10), .clk(Clock), .clr(Reset));
  Register #(.width(32)) register_12 (.D(Res), .en(R11_W), .Q(R11), .clk(Clock), .clr(Reset));
  Register #(.width(32)) register_13 (.D(Res), .en(R12_W), .Q(R12), .clk(Clock), .clr(Reset));
  Register #(.width(32)) register_14 (.D(Res), .en(R13_W), .Q(R13), .clk(Clock), .clr(Reset));
  Register #(.width(32)) register_15 (.D(Res), .en(R14_W), .Q(R14), .clk(Clock), .clr(Reset));
  Register #(.width(32)) register_16 (.D(Res), .en(R15_W), .Q(R15), .clk(Clock), .clr(Reset));
  assign Res = Reg_Write ? Write_Data : 32'bz;  // Controlled_Buffer controlled_buffer_1
  Register #(.width(32)) register_17 (.D(Res), .en(R16_W), .Q(R16), .clk(Clock), .clr(Reset));
  Register #(.width(32)) register_18 (.D(Res), .en(R17_W), .Q(R17), .clk(Clock), .clr(Reset));
  Register #(.width(32)) register_19 (.D(Res), .en(R18_W), .Q(R18), .clk(Clock), .clr(Reset));
  Register #(.width(32)) register_20 (.D(Res), .en(R19_W), .Q(R19), .clk(Clock), .clr(Reset));
  Register #(.width(32)) register_21 (.D(Res), .en(R20_W), .Q(R20), .clk(Clock), .clr(Reset));
  Register #(.width(32)) register_22 (.D(Res), .en(R21_W), .Q(R21), .clk(Clock), .clr(Reset));
  Register #(.width(32)) register_23 (.D(Res), .en(R22_W), .Q(R22), .clk(Clock), .clr(Reset));
  Register #(.width(32)) register_24 (.D(Res), .en(R23_W), .Q(R23), .clk(Clock), .clr(Reset));
  Register #(.width(32)) register_25 (.D(Res), .en(R24_W), .Q(R24), .clk(Clock), .clr(Reset));
  Register #(.width(32)) register_26 (.D(Res), .en(R25_W), .Q(R25), .clk(Clock), .clr(Reset));
  Register #(.width(32)) register_27 (.D(Res), .en(R26_W), .Q(R26), .clk(Clock), .clr(Reset));
  Register #(.width(32)) register_28 (.D(Res), .en(R27_W), .Q(R27), .clk(Clock), .clr(Reset));
  Register #(.width(32)) register_29 (.D(Res), .en(R28_W), .Q(R28), .clk(Clock), .clr(Reset));
  Register #(.width(32)) register_30 (.D(Res), .en(R29_W), .Q(R29), .clk(Clock), .clr(Reset));
  Register #(.width(32)) register_31 (.D(Res), .en(R30_W), .Q(R30), .clk(Clock), .clr(Reset));
  Register #(.width(32)) register_32 (.D(Res), .en(R31_W), .Q(R31), .clk(Clock), .clr(Reset));
  Multiplexer #(.select(5), .width(32), .enable("false")) multiplexer_1 (
    .in0(R0), .in1(R1), .in2(R2), .in3(R3), .in4(R4), .in5(R5), .in6(R6), .in7(R7), .in8(R8), .in9(R9),
    .in10(R10), .in11(R11), .in12(R12), .in13(R13), .in14(R14), .in15(R15), .in16(R16), .in17(R17),
    .in18(R18), .in19(R19), .in20(R20), .in21(R21), .in22(R22), .in23(R23), .in24(R24), .in25(R25),
    .in26(R26), .in27(R27), .in28(R28), .in29(R29), .in30(R30), .in31(R31), .out(RsOut), .sel(Rs));
  Multiplexer #(.select(5), .width(32), .enable("false")) multiplexer_2 (
    .in0(R0), .in1(R1), .in2(R2), .in3(R3), .in4(R4), .in5(R5), .in6(R6), .in7(R7), .in8(R8), .in9(R9),
    .in10(R10), .in11(R11), .in12(R12), .in13(R13), .in14(R14), .in15(R15), .in16(R16), .in17(R17),
    .in18(R18), .in19(R19), .in20(R20), .in21(R21), .in22(R22), .in23(R23), .in24(R24), .in25(R25),
    .in26(R26), .in27(R27), .in28(R28), .in29(R29), .in30(R30), .in31(R31), .out(RtOut), .sel(Rt));
  Demultiplexer #(.select(5), .enable("false")) demultiplexer_1 (
    .out0(R0_W), .out1(R1_W), .out2(R2_W), .out3(R3_W), .out4(R4_W), .out5(R5_W), .out6(R6_W), .out7(R7_W),
    .out8(R8_W), .out9(R9_W), .out10(R10_W), .out11(R11_W), .out12(R12_W), .out13(R13_W), .out14(R14_W),
    .out15(R15_W), .out16(R16_W), .out17(R17_W), .out18(R18_W), .out19(R19_W), .out20(R20_W), .out21(R21_W),
    .out22(R22_W), .out23(R23_W), .out24(R24_W), .out25(R25_W), .out26(R26_W), .out27(R27_W), .out28(R28_W),
    .out29(R29_W), .out30(R30_W), .out31(R31_W), .in(1'b1), .sel(controlled_buffer_2_out));
  assign controlled_buffer_2_out = Reg_Write ? Write_Reg : 5'bz;  // Controlled_Buffer controlled_buffer_2

  // Other names for the same wires on the sheet: R = Reset; RegW = Reg_Write; W_Reg[4:0] = Write_Reg
endmodule

module display (
  input  [5:0] Funct,
  input  [5:0] OpCode,
  input  Tipo_R,
  output Suma,
  output Resta,
  output And,
  output Or,
  output Mult,
  output Beq,
  output AddI,
  output Load,
  output Store,
  output Jump,
  output [27:0] Data
);

  wire comparator_1_eq, comparator_2_eq, comparator_3_eq, comparator_4_eq, comparator_5_eq, comparator_6_eq,
       comparator_7_eq, comparator_8_eq, comparator_9_eq, comparator_10_eq, not_1_out, not_2_out, not_3_out,
       not_4_out, not_5_out;
  wire [3:0] Id;

  Multiplexer #(.width(4), .disabled(0), .enable("false")) multiplexer_1 (
    .in1(4'b0000), .out(Id), .sel(Suma));  // open: in0
  Multiplexer #(.width(4), .disabled(0), .enable("false")) multiplexer_2 (
    .in1(4'b0001), .out(Id), .sel(Resta));  // open: in0
  Multiplexer #(.width(4), .disabled(0), .enable("false")) multiplexer_3 (
    .in1(4'b0010), .out(Id), .sel(And));  // open: in0
  Multiplexer #(.width(4), .disabled(0), .enable("false")) multiplexer_4 (
    .in1(4'b0011), .out(Id), .sel(Or));  // open: in0
  Multiplexer #(.width(4), .disabled(0), .enable("false")) multiplexer_5 (
    .in1(4'b0100), .out(Id), .sel(Mult));  // open: in0
  not not_1 (not_1_out, Tipo_R);
  Comparator #(.width(6)) comparator_1 (.a(OpCode), .b(6'b000100), .eq(comparator_1_eq));  // open: gt, lt
  not not_2 (not_2_out, Tipo_R);
  Comparator #(.width(6)) comparator_2 (.a(OpCode), .b(6'b000010), .eq(comparator_2_eq));  // open: gt, lt
  Multiplexer #(.width(4), .disabled(0), .enable("false")) multiplexer_6 (
    .in1(4'b0101), .out(Id), .sel(Beq));  // open: in0
  Multiplexer #(.width(4), .disabled(0), .enable("false")) multiplexer_7 (
    .in1(4'b0110), .out(Id), .sel(AddI));  // open: in0
  Multiplexer #(.width(4), .disabled(0), .enable("false")) multiplexer_8 (
    .in1(4'b0111), .out(Id), .sel(Load));  // open: in0
  Multiplexer #(.width(4), .disabled(0), .enable("false")) multiplexer_9 (
    .in1(4'b1000), .out(Id), .sel(Store));  // open: in0
  Multiplexer #(.width(4), .disabled(0), .enable("false")) multiplexer_10 (
    .in1(4'b1001), .out(Id), .sel(Jump));  // open: in0
  and and_1 (Beq, not_1_out, comparator_1_eq);
  and and_2 (Jump, not_2_out, comparator_2_eq);
  Comparator #(.width(6)) comparator_3 (.a(Funct), .b(6'b100000), .eq(comparator_3_eq));  // open: gt, lt
  Comparator #(.width(6)) comparator_4 (.a(OpCode), .b(6'b001000), .eq(comparator_4_eq));  // open: gt, lt
  and and_3 (Suma, Tipo_R, comparator_3_eq);
  not not_3 (not_3_out, Tipo_R);
  and and_4 (AddI, not_3_out, comparator_4_eq);
  Comparator #(.width(6)) comparator_5 (.a(Funct), .b(6'b100010), .eq(comparator_5_eq));  // open: gt, lt
  not not_4 (not_4_out, Tipo_R);
  Comparator #(.width(6)) comparator_6 (.a(OpCode), .b(6'b100011), .eq(comparator_6_eq));  // open: gt, lt
  and and_5 (Resta, Tipo_R, comparator_5_eq);
  and and_6 (Load, not_4_out, comparator_6_eq);
  Multiplexer #(.select(4), .width(28), .enable("false")) multiplexer_11 (
    .in0(28'hbfe7c80), .in1(28'hddd7e00), .in2(28'hbf5fc80), .in3(28'hee58000), .in4(28'hb5d5a3c),
    .in5(28'hf8fe780), .in6(28'hbfe7c94), .in7(28'h69deff9), .in8(28'hdcf0000), .in9(28'hc3d6d1f),
    .out(Data), .sel(Id));  // open: in10, in11, in12, in13, in14, in15
  Comparator #(.width(6)) comparator_7 (.a(Funct), .b(6'b100100), .eq(comparator_7_eq));  // open: gt, lt
  Comparator #(.width(6)) comparator_8 (.a(OpCode), .b(6'b101011), .eq(comparator_8_eq));  // open: gt, lt
  and and_7 (And, Tipo_R, comparator_7_eq);
  not not_5 (not_5_out, Tipo_R);
  and and_8 (Store, not_5_out, comparator_8_eq);
  Comparator #(.width(6)) comparator_9 (.a(Funct), .b(6'b100101), .eq(comparator_9_eq));  // open: gt, lt
  and and_9 (Or, Tipo_R, comparator_9_eq);
  Comparator #(.width(6)) comparator_10 (.a(Funct), .b(6'b011000), .eq(comparator_10_eq));  // open: gt, lt
  and and_10 (Mult, Tipo_R, comparator_10_eq);
endmodule

module control (
  input  [5:0] OpCode,
  output Reg_Dest,
  output Branch,
  output MemRead,
  output MemtoReg,
  output [1:0] AluOP,
  output MemWrite,
  output Alu_Src,
  output RegWrite,
  output Jump
);

  wire AddI, or_1_out, TipoR;

  Comparator #(.width(6)) comparator_1 (.a(OpCode), .b({6{1'b0}}), .eq(TipoR));  // open: gt, lt
  Comparator #(.width(6)) comparator_2 (.a(OpCode), .b(6'b001000), .eq(AddI));  // open: gt, lt
  Comparator #(.width(6)) comparator_3 (.a(OpCode), .b(6'b000100), .eq(Branch));  // open: gt, lt
  Comparator #(.width(6)) comparator_4 (.a(OpCode), .b(6'b100011), .eq(MemRead));  // open: gt, lt
  Comparator #(.width(6)) comparator_5 (.a(OpCode), .b(6'b101011), .eq(MemWrite));  // open: gt, lt
  Comparator #(.width(6)) comparator_6 (.a(OpCode), .b(6'b000010), .eq(Jump));  // open: gt, lt
  Multiplexer #(.width(2), .disabled(0), .enable("false")) multiplexer_1 (
    .in1(2'b10), .out(AluOP), .sel(TipoR));  // open: in0
  Multiplexer #(.width(2), .disabled(0), .enable("false")) multiplexer_2 (
    .in1(2'b01), .out(AluOP), .sel(Branch));  // open: in0
  Multiplexer #(.width(2), .disabled(0), .enable("false")) multiplexer_3 (
    .in1(2'b00), .out(AluOP), .sel(or_1_out));  // open: in0
  or or_1 (or_1_out, MemWrite, AddI, MemRead);
  Multiplexer #(.enable("false")) multiplexer_4 (.in0(1'b0), .in1(1'b1), .out(Reg_Dest), .sel(TipoR));
  or or_2 (MemtoReg, MemRead, MemWrite);
  or or_3 (Alu_Src, AddI, MemRead, MemWrite);
  or or_4 (RegWrite, TipoR, AddI, MemRead);

  // Other names for the same wires on the sheet: Beq = Branch; Id[1:0] = AluOP; Load = MemRead; Store = MemWrite
endmodule

module control_alu (
  input  [1:0] AluOP,
  input  [5:0] Funct,
  output [3:0] Alu_Sel
);

  wire And, Beq, comparator_4_eq, comparator_5_eq, comparator_6_eq, comparator_7_eq, comparator_8_eq, Mult,
       Or, Resta, Suma, Tipo_I, Tipo_R;

  Comparator #(.width(2)) comparator_1 (.a(AluOP), .b(2'b10), .eq(Tipo_R));  // open: gt, lt
  Comparator #(.width(2)) comparator_2 (.a(AluOP), .b(2'b01), .eq(Beq));  // open: gt, lt
  Multiplexer #(.width(4), .disabled(0), .enable("false")) multiplexer_1 (
    .in1(4'b0010), .out(Alu_Sel), .sel(Suma));  // open: in0
  Multiplexer #(.width(4), .disabled(0), .enable("false")) multiplexer_2 (
    .in1(4'b0110), .out(Alu_Sel), .sel(Resta));  // open: in0
  Multiplexer #(.width(4), .disabled(0), .enable("false")) multiplexer_3 (
    .in1(4'b0000), .out(Alu_Sel), .sel(And));  // open: in0
  Multiplexer #(.width(4), .disabled(0), .enable("false")) multiplexer_4 (
    .in1(4'b0001), .out(Alu_Sel), .sel(Or));  // open: in0
  Multiplexer #(.width(4), .disabled(0), .enable("false")) multiplexer_5 (
    .in1(4'b0011), .out(Alu_Sel), .sel(Mult));  // open: in0
  Comparator #(.width(2)) comparator_3 (.a(AluOP), .b(2'b00), .eq(Tipo_I));  // open: gt, lt
  Multiplexer #(.width(4), .disabled(0), .enable("false")) multiplexer_6 (
    .in1(4'b0010), .out(Alu_Sel), .sel(Tipo_I));  // open: in0
  Multiplexer #(.width(4), .disabled(0), .enable("false")) multiplexer_7 (
    .in1(4'b0110), .out(Alu_Sel), .sel(Beq));  // open: in0
  Comparator #(.width(6)) comparator_4 (.a(Funct), .b(6'b100000), .eq(comparator_4_eq));  // open: gt, lt
  Comparator #(.width(6)) comparator_5 (.a(Funct), .b(6'b100101), .eq(comparator_5_eq));  // open: gt, lt
  and and_1 (Suma, Tipo_R, comparator_4_eq);
  and and_2 (Or, Tipo_R, comparator_5_eq);
  Comparator #(.width(6)) comparator_6 (.a(Funct), .b(6'b011000), .eq(comparator_6_eq));  // open: gt, lt
  Comparator #(.width(6)) comparator_7 (.a(Funct), .b(6'b100010), .eq(comparator_7_eq));  // open: gt, lt
  and and_3 (Mult, Tipo_R, comparator_6_eq);
  and and_4 (Resta, Tipo_R, comparator_7_eq);
  Comparator #(.width(6)) comparator_8 (.a(Funct), .b(6'b100100), .eq(comparator_8_eq));  // open: gt, lt
  and and_5 (And, Tipo_R, comparator_8_eq);

  // Other names for the same wires on the sheet: Id[3:0] = Alu_Sel
endmodule

module ALU (
  input  [3:0] Alu_Sel,
  input  [31:0] Rs,
  input  [31:0] Rt_Imm,
  output Zero,
  output [31:0] Resul
);

  wire adder_1_cout;
  wire [31:0] AndR, MultR, OrR, SubR, SumaR;

  Adder #(.width(32)) adder_1 (.a(Rt_Imm), .b(Rs), .out(SumaR), .cout(adder_1_cout));  // open: cin
  Subtractor #(.width(32)) subtractor_1 (.a(Rs), .b(Rt_Imm), .out(SubR), .bin(adder_1_cout));  // open: bout
  assign AndR = Rt_Imm & Rs;  // AND_Gate and_1, 32 bits wide
  assign OrR = Rt_Imm | Rs;  // OR_Gate or_1, 32 bits wide
  Multiplier #(.width(32)) multiplier_1 (.a(Rs), .b(Rt_Imm), .out(MultR));  // open: cin, cout
  Multiplexer #(.select(4), .width(32), .enable("false")) multiplexer_1 (
    .in0(AndR), .in1(OrR), .in2(SumaR), .in3(MultR), .in6(SubR), .out(Resul), .sel(Alu_Sel));  // open: in4, in5, in7, in8, in9, in10, in11, in12, in13, in14, in15
  Comparator #(.width(32)) comparator_1 (.a({32{1'b0}}), .b(Resul), .eq(Zero));  // open: gt, lt

  // Other names for the same wires on the sheet: Rt[31:0] = Rt_Imm
endmodule
