// Logisim project decomposer.circ as structural Verilog
module XXX (
  input  [5:0] in_1,
  input  [31:0] in_2
);

  wire comparator_1_eq, comparator_2_eq;

  Comparator #(.width(6)) comparator_1 (.a(in_2[5:0]), .b(in_1), .eq(comparator_1_eq));  // open: gt, lt
  // AND_Gate and_1 has open pins: in0=comparator_1_eq, in1=comparator_2_eq, out=open
  Comparator #(.width(6)) comparator_2 (.a(in_2[31:26]), .b({6{1'b0}}), .eq(comparator_2_eq));  // open: gt, lt

  // Other names for the same wires on the sheet: PCode[5:0] = in_2[5:0]
endmodule
