// Logisim project registers.circ as structural Verilog: 1 circuit, main circuit main
module main (
  input  [4:0] Rs,
  input  [4:0] Rt,
  input  [4:0] Rd,
  input  Clock
);

  wire [31:0] R0, R1, R2, R3, R4, R5, R6, R7, R8, R9, R10, R11, R12, R13, R14, R15, R16, R17, R18, R19, R20,
       R21, R22, R23, R24, R25, R26, R27, R28, R29, R30, R31, RdOut, RsOut, RtOut;

  Register #(.width(32)) register_1 (.Q(R0), .clk(Clock));  // open: D, en, clr
  Register #(.width(32)) register_2 (.Q(R1), .clk(Clock));  // open: D, en, clr
  Register #(.width(32)) register_3 (.Q(R2), .clk(Clock));  // open: D, en, clr
  Register #(.width(32)) register_4 (.Q(R3), .clk(Clock));  // open: D, en, clr
  Register #(.width(32)) register_5 (.Q(R4), .clk(Clock));  // open: D, en, clr
  Register #(.width(32)) register_6 (.Q(R5), .clk(Clock));  // open: D, en, clr
  Register #(.width(32)) register_7 (.Q(R6), .clk(Clock));  // open: D, en, clr
  Register #(.width(32)) register_8 (.Q(R7), .clk(Clock));  // open: D, en, clr
  Register #(.width(32)) register_9 (.Q(R8), .clk(Clock));  // open: D, en, clr
  Register #(.width(32)) register_10 (.Q(R9), .clk(Clock));  // open: D, en, clr
  Register #(.width(32)) register_11 (.Q(R10), .clk(Clock));  // open: D, en, clr
  Register #(.width(32)) register_12 (.Q(R11), .clk(Clock));  // open: D, en, clr
  Register #(.width(32)) register_13 (.Q(R12), .clk(Clock));  // open: D, en, clr
  Register #(.width(32)) register_14 (.Q(R13), .clk(Clock));  // open: D, en, clr
  Register #(.width(32)) register_15 (.Q(R14), .clk(Clock));  // open: D, en, clr
  Register #(.width(32)) register_16 (.Q(R15), .clk(Clock));  // open: D, en, clr
  Register #(.width(32)) register_17 (.Q(R16), .clk(Clock));  // open: D, en, clr
  Register #(.width(32)) register_18 (.Q(R17), .clk(Clock));  // open: D, en, clr
  Register #(.width(32)) register_19 (.Q(R18), .clk(Clock));  // open: D, en, clr
  Register #(.width(32)) register_20 (.Q(R19), .clk(Clock));  // open: D, en, clr
  Register #(.width(32)) register_21 (.Q(R20), .clk(Clock));  // open: D, en, clr
  Register #(.width(32)) register_22 (.Q(R21), .clk(Clock));  // open: D, en, clr
  Register #(.width(32)) register_23 (.Q(R22), .clk(Clock));  // open: D, en, clr
  Register #(.width(32)) register_24 (.Q(R23), .clk(Clock));  // open: D, en, clr
  Register #(.width(32)) register_25 (.Q(R24), .clk(Clock));  // open: D, en, clr
  Register #(.width(32)) register_26 (.Q(R25), .clk(Clock));  // open: D, en, clr
  Register #(.width(32)) register_27 (.Q(R26), .clk(Clock));  // open: D, en, clr
  Register #(.width(32)) register_28 (.Q(R27), .clk(Clock));  // open: D, en, clr
  Register #(.width(32)) register_29 (.Q(R28), .clk(Clock));  // open: D, en, clr
  Register #(.width(32)) register_30 (.Q(R29), .clk(Clock));  // open: D, en, clr
  Register #(.width(32)) register_31 (.Q(R30), .clk(Clock));  // open: D, en, clr
  Register #(.width(32)) register_32 (.Q(R31), .clk(Clock));  // open: D, en, clr
  Multiplexer #(.select(5), .width(32), .enable("false")) multiplexer_1 (
    .in0(R0), .in1(R1), .in2(R2), .in3(R3), .in4(R4), .in5(R5), .in6(R6), .in7(R7), .in8(R8), .in9(R9),
    .in10(R10), .in11(R11), .in12(R12), .in13(R13), .in14(R14), .in15(R15), .in16(R16), .in17(R17),
    .in18(R18), .in19(R19), .in20(R20), .in21(R21), .in22(R22), .in23(R23), .in24(R24), .in25(R25),
    .in26(R26), .in27(R27), .in28(R28), .in29(R29), .in30(R30), .in31(R31), .out(RsOut), .sel(Rs));
  Multiplexer #(.select(5), .width(32), .enable("false")) multiplexer_2 (
    .in0(R0), .in1(R1), .in2(R2), .in3(R3), .in4(R4), .in5(R5), .in6(R6), .in7(R7), .in8(R8), .in9(R9),
    .in10(R10), .in11(R11), .in12(R12), .in13(R13), .in14(R14), .in15(R15), .in16(R16), .in17(R17),
    .in18(R18), .in19(R19), .in20(R20), .in21(R21), .in22(R22), .in23(R23), .in24(R24), .in25(R25),
    .in26(R26), .in27(R27), .in28(R28), .in29(R29), .in30(R30), .in31(R31), .out(RtOut), .sel(Rt));
  Multiplexer #(.select(5), .width(32), .enable("false")) multiplexer_3 (
    .in0(R0), .in1(R1), .in2(R2), .in3(R3), .in4(R4), .in5(R5), .in6(R6), .in7(R7), .in8(R8), .in9(R9),
    .in10(R10), .in11(R11), .in12(R12), .in13(R13), .in14(R14), .in15(R15), .in16(R16), .in17(R17),
    .in18(R18), .in19(R19), .in20(R20), .in21(R21), .in22(R22), .in23(R23), .in24(R24), .in25(R25),
    .in26(R26), .in27(R27), .in28(R28), .in29(R29), .in30(R30), .in31(R31), .out(RdOut), .sel(Rd));
endmodule
